// Logisim project cpu.circ as structural Verilog
module alu (
  input  [15:0] in_1,
  input  [15:0] in_2,
  input  [2:0] in_3,
  output [15:0] out_4
);

  wire [15:0] adder_1_out, nand_1_out, negator_1_out, shifter_1_out, shifter_2_out, subtractor_1_out;

  Shifter #(.width(16), .shift("lr")) shifter_1 (.in(in_1), .\dist (4'b0001), .out(shifter_1_out));
  Shifter #(.width(16)) shifter_2 (.in(in_1), .\dist (4'b0001), .out(shifter_2_out));
  Adder #(.width(16)) adder_1 (.a(in_1), .b(in_2), .out(adder_1_out), .cin(1'b0));  // open: cout
  Subtractor #(.width(16)) subtractor_1 (.a(in_1), .b(in_2), .out(subtractor_1_out), .bin(1'b0));  // open: bout
  assign nand_1_out = ~(in_1 & in_2);  // NAND_Gate nand_1, 16 bits wide
  Negator #(.width(16)) negator_1 (.in(in_1), .out(negator_1_out));
  Multiplexer #(.select(3), .width(16), .enable("false")) multiplexer_1 (
    .in0(shifter_1_out), .in1(shifter_2_out), .in2(adder_1_out), .in3(subtractor_1_out), .in4(nand_1_out),
    .in5(negator_1_out), .in6({16{1'b0}}), .in7(16'h1), .out(out_4), .sel(in_3));

  // Notes on the sheet:
  //   Source
  //   Destination
endmodule
